# Fritzing sketch Fritzingdiagram Zumo (saved by Fritzing 0.9.3b)
breadboards: 2

parts:
  Part1 = Arduino Uno (Rev3) - ICSP
  hc-sr1 = hc-sr04
  Part2 = Bluetooth HC-05 Macho  # not connected

nets:
  N1: Part1.D3_PWM, hc-sr1.Echo
  N2: Part1.D6_PWM, hc-sr1.Trig
  5V: Part1.5V, hc-sr1.VCC
  GND: Part1.GND, hc-sr1.GND
